// Logisim project laberinto.circ as structural Verilog: 8 circuits, main circuit Siguiente Posicion
module Siguiente_Posicion (
  input  [2:0] in_1,
  input  [2:0] in_2,
  output [2:0] out_3,
  output [2:0] out_4
);

  wire and_1_out, and_2_out, and_3_out, and_4_out, and_5_out, and_6_out, and_7_out, and_8_out, and_9_out,
       and_10_out, and_11_out, and_12_out, and_13_out, and_14_out, and_15_out, and_16_out, and_17_out,
       and_18_out, and_19_out, and_20_out, and_21_out, and_22_out, and_23_out, and_24_out, and_25_out,
       and_26_out, and_27_out, and_28_out, and_29_out, and_30_out, and_31_out, and_32_out, and_33_out,
       and_34_out, and_35_out, and_36_out, and_37_out, and_38_out, and_39_out, and_40_out, and_41_out,
       and_42_out, and_43_out, and_44_out, and_45_out, and_46_out, and_47_out, and_48_out, and_49_out,
       and_50_out, and_51_out, and_52_out, and_53_out, and_54_out, and_55_out, and_56_out, and_57_out,
       and_58_out, and_59_out, and_60_out, and_61_out, and_62_out, and_63_out, and_64_out, and_65_out,
       and_66_out, and_67_out, not_1_out, not_2_out, not_3_out, not_4_out, not_5_out, not_6_out, not_7_out,
       not_8_out, not_9_out, not_10_out, not_11_out, not_12_out, not_13_out, not_14_out, not_15_out,
       not_16_out, not_17_out, not_18_out, not_19_out, not_20_out, not_21_out, not_22_out, not_23_out,
       not_24_out, not_25_out, not_26_out, not_27_out, not_28_out, not_29_out, not_30_out, not_31_out,
       not_32_out, not_33_out, not_34_out, not_35_out, not_36_out, not_37_out, not_38_out, not_39_out,
       not_40_out, not_41_out, not_42_out, not_43_out, not_44_out, not_45_out, not_46_out, not_47_out,
       not_48_out, not_49_out, not_50_out, not_51_out, not_52_out, not_53_out, not_54_out, not_55_out,
       not_56_out, not_57_out, not_58_out, not_59_out, not_60_out, not_61_out, not_62_out, not_63_out,
       not_64_out, not_65_out, not_66_out, not_67_out, not_68_out, not_69_out, not_70_out, not_71_out,
       not_72_out, not_73_out, not_74_out, not_75_out, not_76_out, not_77_out, not_78_out, not_79_out,
       not_80_out, not_81_out, not_82_out, not_83_out, not_84_out, not_85_out, not_86_out, not_87_out,
       not_88_out, not_89_out, not_90_out, not_91_out, not_92_out, not_93_out, not_94_out, not_95_out,
       not_96_out, not_97_out, not_98_out, not_99_out, not_100_out, not_101_out, not_102_out, not_103_out,
       not_104_out, not_105_out, not_106_out, not_107_out, not_108_out, not_109_out, not_110_out,
       not_111_out, not_112_out, not_113_out, not_114_out, not_115_out, not_116_out;

  not not_1 (not_1_out, in_1[1]);
  not not_2 (not_2_out, in_1[0]);
  not not_3 (not_3_out, in_2[1]);
  not not_4 (not_4_out, in_1[0]);
  not not_5 (not_5_out, in_2[2]);
  not not_6 (not_6_out, in_2[0]);
  not not_7 (not_7_out, in_1[1]);
  not not_8 (not_8_out, in_1[0]);
  not not_9 (not_9_out, in_1[1]);
  not not_10 (not_10_out, in_2[1]);
  not not_11 (not_11_out, in_1[1]);
  not not_12 (not_12_out, in_2[0]);
  not not_13 (not_13_out, in_1[1]);
  not not_14 (not_14_out, in_2[2]);
  not not_15 (not_15_out, in_1[2]);
  not not_16 (not_16_out, in_2[1]);
  not not_17 (not_17_out, in_1[2]);
  not not_18 (not_18_out, in_2[0]);
  not not_19 (not_19_out, in_2[2]);
  not not_20 (not_20_out, in_2[1]);
  not not_21 (not_21_out, in_1[2]);
  not not_22 (not_22_out, in_1[1]);
  not not_23 (not_23_out, in_1[0]);
  not not_24 (not_24_out, in_2[1]);
  not not_25 (not_25_out, in_1[0]);
  not not_26 (not_26_out, in_1[2]);
  not not_27 (not_27_out, in_1[1]);
  not not_28 (not_28_out, in_1[2]);
  not not_29 (not_29_out, in_1[0]);
  not not_30 (not_30_out, in_2[2]);
  not not_31 (not_31_out, in_1[2]);
  not not_32 (not_32_out, in_1[0]);
  not not_33 (not_33_out, in_1[2]);
  not not_34 (not_34_out, in_1[0]);
  not not_35 (not_35_out, in_2[1]);
  not not_36 (not_36_out, in_1[2]);
  not not_37 (not_37_out, in_2[2]);
  not not_38 (not_38_out, in_1[0]);
  not not_39 (not_39_out, in_2[0]);
  not not_40 (not_40_out, in_1[0]);
  not not_41 (not_41_out, in_2[2]);
  not not_42 (not_42_out, in_2[1]);
  not not_43 (not_43_out, in_2[0]);
  not not_44 (not_44_out, in_2[1]);
  not not_45 (not_45_out, in_1[2]);
  not not_46 (not_46_out, in_1[0]);
  not not_47 (not_47_out, in_2[2]);
  not not_48 (not_48_out, in_1[2]);
  not not_49 (not_49_out, in_1[1]);
  not not_50 (not_50_out, in_2[2]);
  not not_51 (not_51_out, in_2[2]);
  not not_52 (not_52_out, in_1[2]);
  not not_53 (not_53_out, in_1[1]);
  not not_54 (not_54_out, in_2[0]);
  not not_55 (not_55_out, in_1[1]);
  not not_56 (not_56_out, in_1[0]);
  not not_57 (not_57_out, in_2[1]);
  not not_58 (not_58_out, in_1[2]);
  not not_59 (not_59_out, in_1[1]);
  not not_60 (not_60_out, in_2[0]);
  not not_61 (not_61_out, in_1[1]);
  not not_62 (not_62_out, in_2[0]);
  not not_63 (not_63_out, in_1[0]);
  not not_64 (not_64_out, in_2[2]);
  not not_65 (not_65_out, in_1[0]);
  not not_66 (not_66_out, in_2[0]);
  not not_67 (not_67_out, in_2[2]);
  not not_68 (not_68_out, in_2[1]);
  not not_69 (not_69_out, in_2[0]);
  not not_70 (not_70_out, in_2[1]);
  not not_71 (not_71_out, in_2[2]);
  not not_72 (not_72_out, in_2[1]);
  not not_73 (not_73_out, in_2[0]);
  not not_74 (not_74_out, in_2[2]);
  not not_75 (not_75_out, in_2[1]);
  not not_76 (not_76_out, in_1[0]);
  not not_77 (not_77_out, in_2[0]);
  not not_78 (not_78_out, in_1[2]);
  and and_1 (and_1_out, not_78_out, in_2[2]);
  not not_79 (not_79_out, in_1[1]);
  and and_2 (and_2_out, not_79_out, in_2[2]);
  not not_80 (not_80_out, in_1[0]);
  and and_3 (and_3_out, not_80_out, in_2[2]);
  and and_4 (and_4_out, in_2[2], in_2[0]);
  and and_5 (and_5_out, in_2[2], in_2[1]);
  not not_81 (not_81_out, in_1[2]);
  and and_6 (and_6_out, not_81_out, in_1[1], in_2[1]);
  and and_7 (and_7_out, in_1[1], in_2[1], in_2[0]);
  not not_82 (not_82_out, in_1[1]);
  not not_83 (not_83_out, in_1[0]);
  not not_84 (not_84_out, in_2[2]);
  not not_85 (not_85_out, in_1[0]);
  not not_86 (not_86_out, in_2[2]);
  not not_87 (not_87_out, in_1[1]);
  not not_88 (not_88_out, in_1[1]);
  not not_89 (not_89_out, in_2[1]);
  not not_90 (not_90_out, in_2[0]);
  not not_91 (not_91_out, in_1[1]);
  not not_92 (not_92_out, in_2[0]);
  not not_93 (not_93_out, in_2[2]);
  not not_94 (not_94_out, in_2[0]);
  not not_95 (not_95_out, in_2[2]);
  not not_96 (not_96_out, in_1[2]);
  not not_97 (not_97_out, in_1[1]);
  not not_98 (not_98_out, in_1[2]);
  not not_99 (not_99_out, in_1[1]);
  not not_100 (not_100_out, in_1[1]);
  not not_101 (not_101_out, in_1[0]);
  not not_102 (not_102_out, in_2[2]);
  not not_103 (not_103_out, in_1[1]);
  not not_104 (not_104_out, in_2[1]);
  not not_105 (not_105_out, in_1[1]);
  not not_106 (not_106_out, in_2[1]);
  not not_107 (not_107_out, in_1[1]);
  not not_108 (not_108_out, in_1[2]);
  not not_109 (not_109_out, in_2[2]);
  not not_110 (not_110_out, in_2[1]);
  not not_111 (not_111_out, in_1[0]);
  not not_112 (not_112_out, in_2[2]);
  not not_113 (not_113_out, in_2[2]);
  not not_114 (not_114_out, in_2[1]);
  not not_115 (not_115_out, in_2[0]);
  not not_116 (not_116_out, in_2[0]);
  and and_8 (and_8_out, not_1_out, not_2_out, not_3_out, in_2[0]);
  and and_9 (and_9_out, not_4_out, not_5_out, in_2[1], not_6_out);
  and and_10 (and_10_out, not_7_out, not_8_out, in_2[2]);
  and and_11 (and_11_out, not_9_out, in_2[2], not_10_out, in_2[0]);
  and and_12 (and_12_out, not_11_out, in_2[2], in_2[1], not_12_out);
  and and_13 (and_13_out, not_13_out, in_1[0], not_14_out, in_2[1], in_2[0]);
  and and_14 (and_14_out, not_15_out, in_1[1], in_1[0], not_16_out);
  and and_15 (and_15_out, not_17_out, in_1[1], in_1[0], not_18_out);
  and and_16 (and_16_out, in_1[1], in_1[0], not_19_out, not_20_out);
  and and_17 (and_17_out, not_21_out, in_1[1], in_1[0], in_2[2]);
  and and_18 (and_18_out, in_1[2], not_22_out, not_23_out, not_24_out);
  and and_19 (and_19_out, in_1[2], not_25_out, in_2[2]);
  and and_20 (and_20_out, in_1[2], in_1[0], in_2[0]);
  and and_21 (and_21_out, in_1[2], in_1[0], in_2[1]);
  and and_22 (and_22_out, not_26_out, not_27_out, in_2[0]);
  and and_23 (and_23_out, not_28_out, not_29_out, in_2[1]);
  and and_24 (and_24_out, not_30_out, in_2[1], in_2[0]);
  and and_25 (and_25_out, not_31_out, not_32_out, in_2[2]);
  and and_26 (and_26_out, not_33_out, in_2[2], in_2[0]);
  and and_27 (and_27_out, in_1[1], not_34_out, not_35_out);
  and and_28 (and_28_out, not_36_out, in_1[1], not_37_out, in_2[1]);
  and and_29 (and_29_out, in_1[1], not_38_out, in_2[2], not_39_out);
  and and_30 (and_30_out, in_1[2], not_40_out, not_41_out, not_42_out, not_43_out);
  and and_31 (and_31_out, in_1[2], in_1[0], not_44_out, in_2[0]);
  and and_32 (and_32_out, in_1[2], in_1[1], in_1[0], in_2[1]);
  and and_33 (and_33_out, not_45_out, not_46_out, not_47_out, in_2[0]);
  and and_34 (and_34_out, not_48_out, not_49_out, not_50_out, in_2[1]);
  and and_35 (and_35_out, not_51_out, in_2[1], in_2[0]);
  and and_36 (and_36_out, not_52_out, not_53_out, in_2[2], not_54_out);
  and and_37 (and_37_out, not_55_out, not_56_out, in_2[2], not_57_out, in_2[0]);
  and and_38 (and_38_out, not_58_out, not_59_out, in_1[0], not_60_out);
  and and_39 (and_39_out, not_61_out, in_1[0], in_2[2], not_62_out);
  and and_40 (and_40_out, in_1[1], not_63_out, not_64_out);
  and and_41 (and_41_out, in_1[1], not_65_out, not_66_out);
  and and_42 (and_42_out, in_1[1], not_67_out, not_68_out, not_69_out);
  and and_43 (and_43_out, in_1[1], in_1[0], in_2[2], not_70_out, in_2[0]);
  and and_44 (and_44_out, in_1[2], not_71_out, not_72_out, not_73_out);
  and and_45 (and_45_out, in_1[2], in_1[1], not_74_out, not_75_out);
  and and_46 (and_46_out, in_1[2], in_1[1], not_76_out, in_2[1]);
  and and_47 (and_47_out, in_1[2], in_1[1], in_2[2], in_2[1], not_77_out);
  and and_48 (and_48_out, not_82_out, not_83_out, not_84_out, in_2[0]);
  and and_49 (and_49_out, not_85_out, not_86_out, in_2[1]);
  and and_50 (and_50_out, not_87_out, in_2[1], in_2[0]);
  and and_51 (and_51_out, not_88_out, in_1[0], not_89_out, not_90_out);
  and and_52 (and_52_out, not_91_out, in_1[0], in_2[2], not_92_out);
  and and_53 (and_53_out, in_1[1], not_93_out, not_94_out);
  and and_54 (and_54_out, in_1[1], in_2[2], in_2[1]);
  and and_55 (and_55_out, in_1[2], not_95_out);
  and and_56 (and_56_out, not_96_out, not_97_out, in_2[0]);
  and and_57 (and_57_out, not_98_out, not_99_out, in_2[1]);
  and and_58 (and_58_out, not_100_out, not_101_out, not_102_out, in_2[1]);
  and and_59 (and_59_out, not_103_out, in_2[2], not_104_out);
  and and_60 (and_60_out, not_105_out, in_1[0], not_106_out);
  and and_61 (and_61_out, not_107_out, in_1[0], in_2[0]);
  and and_62 (and_62_out, in_1[0], in_2[2], in_2[1], in_2[0]);
  and and_63 (and_63_out, not_108_out, in_1[1], not_109_out, not_110_out);
  and and_64 (and_64_out, in_1[1], not_111_out, not_112_out, in_2[0]);
  and and_65 (and_65_out, in_1[2], not_113_out, not_114_out, not_115_out);
  and and_66 (and_66_out, in_1[2], in_2[2], in_2[1], not_116_out);
  and and_67 (and_67_out, in_1[2], in_1[1], in_2[2], in_2[1]);
  or or_1 (out_3[2], and_8_out, and_9_out, and_10_out, and_11_out, and_12_out, and_13_out, and_14_out, and_15_out, and_16_out, and_17_out, and_18_out, and_19_out, and_20_out, and_21_out);
  or or_2 (out_3[1], and_22_out, and_23_out, and_24_out, and_25_out, and_26_out, and_27_out, and_28_out, and_29_out, and_30_out, and_31_out, and_32_out);
  or or_3 (out_3[0], and_33_out, and_34_out, and_35_out, and_36_out, and_37_out, and_38_out, and_39_out, and_40_out, and_41_out, and_42_out, and_43_out, and_44_out, and_45_out, and_46_out, and_47_out);
  or or_4 (out_4[2], and_1_out, and_2_out, and_3_out, and_4_out, and_5_out, and_6_out, and_7_out);
  or or_5 (out_4[1], and_48_out, and_49_out, and_50_out, and_51_out, and_52_out, and_53_out, and_54_out, and_55_out);
  or or_6 (out_4[0], and_56_out, and_57_out, and_58_out, and_59_out, and_60_out, and_61_out, and_62_out, and_63_out, and_64_out, and_65_out, and_66_out, and_67_out);
endmodule

module Flip_Flip_D (
  input  in_1,
  output out_2,
  output out_3
);

  wire clock_1_out, nand_1_out, nand_2_out, not_1_out;

  Clock clock_1 (.out(clock_1_out));
  not not_1 (not_1_out, in_1);
  nand nand_1 (nand_1_out, in_1, clock_1_out);
  nand nand_2 (nand_2_out, clock_1_out, not_1_out);
  nand nand_3 (out_2, nand_1_out, out_3);
  nand nand_4 (out_3, out_2, nand_2_out);
endmodule

module Memory (
  input  [2:0] in_1,
  input  [2:0] in_2,
  output [2:0] out_3,
  output [2:0] out_4
);

  Flip_Flip_D flip_flip_d_1 (.in_1(in_1[2]), .out_2(out_3[2]));  // open: out_3
  Flip_Flip_D flip_flip_d_2 (.in_1(in_1[1]), .out_2(out_3[1]));  // open: out_3
  Flip_Flip_D flip_flip_d_3 (.in_1(in_1[0]), .out_2(out_3[0]));  // open: out_3
  Flip_Flip_D flip_flip_d_4 (.in_1(in_2[2]), .out_2(out_4[2]));  // open: out_3
  Flip_Flip_D flip_flip_d_5 (.in_1(in_2[1]), .out_2(out_4[1]));  // open: out_3
  Flip_Flip_D flip_flip_d_6 (.in_1(in_2[0]), .out_2(out_4[0]));  // open: out_3
endmodule

module Salida (
  input  [2:0] in_1,
  input  [2:0] in_2,
  output [3:0] out_3
);

  wire and_1_out, and_2_out, and_3_out, and_4_out, and_5_out, and_6_out, and_7_out, and_8_out, and_9_out,
       and_10_out, and_11_out, and_12_out, and_13_out, and_14_out, and_15_out, and_16_out, and_17_out,
       and_18_out, and_19_out, and_20_out, and_21_out, not_1_out, not_2_out, not_3_out, not_4_out, not_5_out,
       not_6_out, not_7_out, not_8_out, not_9_out, not_10_out, not_11_out, not_12_out, not_13_out,
       not_14_out, not_15_out, not_16_out, not_17_out, not_18_out, not_19_out, not_20_out, not_21_out,
       not_22_out, not_23_out, not_24_out, not_25_out, not_26_out, not_27_out, not_28_out, not_29_out,
       not_30_out, not_31_out, not_32_out, not_33_out, not_34_out, not_35_out, not_36_out, not_37_out,
       not_38_out, not_39_out, not_40_out, not_41_out, not_42_out, not_43_out;

  not not_1 (not_1_out, in_1[2]);
  not not_2 (not_2_out, in_1[1]);
  not not_3 (not_3_out, in_1[0]);
  not not_4 (not_4_out, in_1[1]);
  not not_5 (not_5_out, in_2[2]);
  not not_6 (not_6_out, in_2[2]);
  not not_7 (not_7_out, in_2[0]);
  not not_8 (not_8_out, in_2[1]);
  not not_9 (not_9_out, in_2[0]);
  not not_10 (not_10_out, in_1[1]);
  not not_11 (not_11_out, in_1[2]);
  not not_12 (not_12_out, in_1[1]);
  not not_13 (not_13_out, in_2[0]);
  not not_14 (not_14_out, in_1[2]);
  not not_15 (not_15_out, in_1[0]);
  not not_16 (not_16_out, in_1[1]);
  not not_17 (not_17_out, in_1[0]);
  not not_18 (not_18_out, in_2[1]);
  not not_19 (not_19_out, in_2[1]);
  not not_20 (not_20_out, in_2[0]);
  not not_21 (not_21_out, in_1[1]);
  not not_22 (not_22_out, in_1[0]);
  not not_23 (not_23_out, in_2[2]);
  not not_24 (not_24_out, in_2[0]);
  not not_25 (not_25_out, in_1[1]);
  not not_26 (not_26_out, in_2[1]);
  not not_27 (not_27_out, in_2[0]);
  not not_28 (not_28_out, in_1[2]);
  not not_29 (not_29_out, in_2[2]);
  not not_30 (not_30_out, in_2[2]);
  not not_31 (not_31_out, in_2[1]);
  not not_32 (not_32_out, in_2[0]);
  not not_33 (not_33_out, in_1[2]);
  not not_34 (not_34_out, in_2[2]);
  not not_35 (not_35_out, in_2[1]);
  not not_36 (not_36_out, in_1[2]);
  not not_37 (not_37_out, in_1[1]);
  not not_38 (not_38_out, in_1[1]);
  not not_39 (not_39_out, in_2[1]);
  not not_40 (not_40_out, in_1[2]);
  not not_41 (not_41_out, in_2[0]);
  not not_42 (not_42_out, in_2[1]);
  not not_43 (not_43_out, in_2[0]);
  and and_1 (and_1_out, not_1_out, not_2_out, not_3_out);
  and and_2 (and_2_out, not_4_out, not_5_out, in_2[1], in_2[0]);
  and and_3 (and_3_out, in_1[1], not_6_out, not_7_out);
  and and_4 (and_4_out, in_1[2], in_1[0], not_8_out, not_9_out);
  and and_5 (and_5_out, in_1[2], not_10_out, in_1[0], in_2[1]);
  and and_6 (and_6_out, in_1[2], in_1[1], in_2[1], in_2[0]);
  and and_7 (and_7_out, not_11_out, not_12_out, not_13_out);
  and and_8 (and_8_out, not_14_out, not_15_out, in_2[2], in_2[0]);
  and and_9 (and_9_out, not_16_out, not_17_out, in_2[2], in_2[1]);
  and and_10 (and_10_out, in_1[1], in_2[2], not_18_out, in_2[0]);
  and and_11 (and_11_out, in_1[2], in_1[0], not_19_out, not_20_out);
  and and_12 (and_12_out, not_21_out, not_22_out, not_23_out, not_24_out);
  and and_13 (and_13_out, not_25_out, not_26_out, not_27_out);
  and and_14 (and_14_out, not_28_out, in_1[1], not_29_out, in_2[1]);
  and and_15 (and_15_out, in_1[2], not_30_out, not_31_out);
  and and_16 (and_16_out, in_1[2], in_1[0], in_2[2], not_32_out);
  and and_17 (and_17_out, not_33_out, not_34_out, not_35_out);
  and and_18 (and_18_out, not_36_out, not_37_out, in_2[2]);
  and and_19 (and_19_out, not_38_out, in_2[2], not_39_out, in_2[0]);
  and and_20 (and_20_out, not_40_out, in_1[1], not_41_out);
  and and_21 (and_21_out, in_1[1], not_42_out, not_43_out);
  or or_1 (out_3[3], and_1_out, and_2_out, and_3_out, and_4_out, and_5_out, and_6_out);
  or or_2 (out_3[2], and_7_out, and_8_out, and_9_out, and_10_out, and_11_out);
  or or_3 (out_3[1], and_12_out, and_13_out, and_14_out, and_15_out, and_16_out);
  or or_4 (out_3[0], and_17_out, and_18_out, and_19_out, and_20_out, and_21_out);
endmodule

module Memoria_Final (
  input  [2:0] in_1,
  input  [2:0] in_2,
  input  [2:0] in_3,
  input  [2:0] in_4,
  input  [2:0] in_5,
  input  [2:0] in_6,
  input  [2:0] in_7,
  input  [2:0] in_8,
  input  [2:0] in_9,
  input  [2:0] in_10,
  input  [2:0] in_11,
  input  [2:0] in_12,
  input  [2:0] in_13,
  input  [2:0] in_14,
  input  [2:0] in_15,
  input  [2:0] in_16,
  input  [2:0] in_17,
  input  [2:0] in_18,
  input  [2:0] in_19,
  input  [2:0] in_20,
  input  [2:0] in_21,
  input  [2:0] in_22,
  input  [2:0] in_23,
  input  [2:0] in_24,
  input  [2:0] in_25,
  input  [2:0] in_26,
  input  [2:0] in_27,
  input  [2:0] in_28,
  input  [2:0] in_29,
  input  [2:0] in_30,
  output [2:0] _1,
  output [2:0] out_32,
  output [2:0] _2,
  output [2:0] out_34,
  output [2:0] _3,
  output [2:0] out_36,
  output [2:0] _4,
  output [2:0] out_38,
  output [2:0] _5,
  output [2:0] out_40,
  output [2:0] _6,
  output [2:0] out_42,
  output [2:0] _7,
  output [2:0] out_44,
  output [2:0] _8,
  output [2:0] out_46,
  output [2:0] _9,
  output [2:0] out_48,
  output [2:0] _10,
  output [2:0] out_50,
  output [2:0] _11,
  output [2:0] out_52,
  output [2:0] _12,
  output [2:0] out_54,
  output [2:0] _13,
  output [2:0] out_56,
  output [2:0] _14,
  output [2:0] out_58,
  output [2:0] _15,
  output [2:0] out_60
);

  Memory memory_1 (.in_1(in_1), .in_2(in_2), .out_3(_1), .out_4(out_32));
  Memory memory_2 (.in_1(in_3), .in_2(in_4), .out_3(_2), .out_4(out_34));
  Memory memory_3 (.in_1(in_5), .in_2(in_6), .out_3(_3), .out_4(out_36));
  Memory memory_4 (.in_1(in_7), .in_2(in_8), .out_3(_4), .out_4(out_38));
  Memory memory_5 (.in_1(in_9), .in_2(in_10), .out_3(_5), .out_4(out_40));
  Memory memory_6 (.in_1(in_11), .in_2(in_12), .out_3(_6), .out_4(out_42));
  Memory memory_7 (.in_1(in_13), .in_2(in_14), .out_3(_7), .out_4(out_44));
  Memory memory_8 (.in_1(in_15), .in_2(in_16), .out_3(_8), .out_4(out_46));
  Memory memory_9 (.in_1(in_17), .in_2(in_18), .out_3(_9), .out_4(out_48));
  Memory memory_10 (.in_1(in_19), .in_2(in_20), .out_3(_10), .out_4(out_50));
  Memory memory_11 (.in_1(in_21), .in_2(in_22), .out_3(_11), .out_4(out_52));
  Memory memory_12 (.in_1(in_23), .in_2(in_24), .out_3(_12), .out_4(out_54));
  Memory memory_13 (.in_1(in_25), .in_2(in_26), .out_3(_13), .out_4(out_56));
  Memory memory_14 (.in_1(in_27), .in_2(in_28), .out_3(_14), .out_4(out_58));
  Memory memory_15 (.in_1(in_29), .in_2(in_30), .out_3(_15), .out_4(out_60));
endmodule

module main (
  input  [2:0] in_1,
  input  [2:0] in_2,
  output [3:0] out_3,
  output [3:0] out_4,
  output [3:0] out_5,
  output [3:0] out_6,
  output [3:0] out_7,
  output [3:0] out_8,
  output [3:0] out_9,
  output [3:0] out_10,
  output [3:0] out_11,
  output [3:0] out_12,
  output [3:0] out_13,
  output [3:0] out_14,
  output [3:0] out_15,
  output [3:0] out_16,
  output [3:0] out_17
);

  wire [2:0] memoria_final_1__1, memoria_final_1__2, memoria_final_1__3, memoria_final_1__4,
       memoria_final_1__5, memoria_final_1__6, memoria_final_1__7, memoria_final_1__8, memoria_final_1__9,
       memoria_final_1__10, memoria_final_1__11, memoria_final_1__12, memoria_final_1__13,
       memoria_final_1__14, memoria_final_1_out_32, memoria_final_1_out_34, memoria_final_1_out_36,
       memoria_final_1_out_38, memoria_final_1_out_40, memoria_final_1_out_42, memoria_final_1_out_44,
       memoria_final_1_out_46, memoria_final_1_out_48, memoria_final_1_out_50, memoria_final_1_out_52,
       memoria_final_1_out_54, memoria_final_1_out_56, memoria_final_1_out_58, siguiente_posicion_final_1__1,
       siguiente_posicion_final_1__2, siguiente_posicion_final_1__3, siguiente_posicion_final_1__4,
       siguiente_posicion_final_1__5, siguiente_posicion_final_1__6, siguiente_posicion_final_1__7,
       siguiente_posicion_final_1__8, siguiente_posicion_final_1__9, siguiente_posicion_final_1__10,
       siguiente_posicion_final_1__11, siguiente_posicion_final_1__12, siguiente_posicion_final_1__13,
       siguiente_posicion_final_1__14, siguiente_posicion_final_1__15, siguiente_posicion_final_1_out_32,
       siguiente_posicion_final_1_out_34, siguiente_posicion_final_1_out_36,
       siguiente_posicion_final_1_out_38, siguiente_posicion_final_1_out_40,
       siguiente_posicion_final_1_out_42, siguiente_posicion_final_1_out_44,
       siguiente_posicion_final_1_out_46, siguiente_posicion_final_1_out_48,
       siguiente_posicion_final_1_out_50, siguiente_posicion_final_1_out_52,
       siguiente_posicion_final_1_out_54, siguiente_posicion_final_1_out_56,
       siguiente_posicion_final_1_out_58, siguiente_posicion_final_1_out_60;

  Siguiente_Posicion_Final siguiente_posicion_final_1 (
    .in_1(in_1), .in_2(in_2), .in_3(memoria_final_1__1), .in_4(memoria_final_1_out_32),
    .in_5(memoria_final_1__2), .in_6(memoria_final_1_out_34), .in_7(memoria_final_1__3),
    .in_8(memoria_final_1_out_36), .in_9(memoria_final_1__4), .in_10(memoria_final_1_out_38),
    .in_11(memoria_final_1__5), .in_12(memoria_final_1_out_40), .in_13(memoria_final_1__6),
    .in_14(memoria_final_1_out_42), .in_15(memoria_final_1__7), .in_16(memoria_final_1_out_44),
    .in_17(memoria_final_1__8), .in_18(memoria_final_1_out_46), .in_19(memoria_final_1__9),
    .in_20(memoria_final_1_out_48), .in_21(memoria_final_1__10), .in_22(memoria_final_1_out_50),
    .in_23(memoria_final_1__11), .in_24(memoria_final_1_out_52), .in_25(memoria_final_1__12),
    .in_26(memoria_final_1_out_54), .in_27(memoria_final_1__13), .in_28(memoria_final_1_out_56),
    .in_29(memoria_final_1__14), .in_30(memoria_final_1_out_58), ._1(siguiente_posicion_final_1__1),
    .out_32(siguiente_posicion_final_1_out_32), ._2(siguiente_posicion_final_1__2),
    .out_34(siguiente_posicion_final_1_out_34), ._3(siguiente_posicion_final_1__3),
    .out_36(siguiente_posicion_final_1_out_36), ._4(siguiente_posicion_final_1__4),
    .out_38(siguiente_posicion_final_1_out_38), ._5(siguiente_posicion_final_1__5),
    .out_40(siguiente_posicion_final_1_out_40), ._6(siguiente_posicion_final_1__6),
    .out_42(siguiente_posicion_final_1_out_42), ._7(siguiente_posicion_final_1__7),
    .out_44(siguiente_posicion_final_1_out_44), ._8(siguiente_posicion_final_1__8),
    .out_46(siguiente_posicion_final_1_out_46), ._9(siguiente_posicion_final_1__9),
    .out_48(siguiente_posicion_final_1_out_48), ._10(siguiente_posicion_final_1__10),
    .out_50(siguiente_posicion_final_1_out_50), ._11(siguiente_posicion_final_1__11),
    .out_52(siguiente_posicion_final_1_out_52), ._12(siguiente_posicion_final_1__12),
    .out_54(siguiente_posicion_final_1_out_54), ._13(siguiente_posicion_final_1__13),
    .out_56(siguiente_posicion_final_1_out_56), ._14(siguiente_posicion_final_1__14),
    .out_58(siguiente_posicion_final_1_out_58), ._15(siguiente_posicion_final_1__15),
    .out_60(siguiente_posicion_final_1_out_60));
  Memoria_Final memoria_final_1 (
    .in_1(siguiente_posicion_final_1__1), .in_2(siguiente_posicion_final_1_out_32),
    .in_3(siguiente_posicion_final_1__2), .in_4(siguiente_posicion_final_1_out_34),
    .in_5(siguiente_posicion_final_1__3), .in_6(siguiente_posicion_final_1_out_36),
    .in_7(siguiente_posicion_final_1__4), .in_8(siguiente_posicion_final_1_out_38),
    .in_9(siguiente_posicion_final_1__5), .in_10(siguiente_posicion_final_1_out_40),
    .in_11(siguiente_posicion_final_1__6), .in_12(siguiente_posicion_final_1_out_42),
    .in_13(siguiente_posicion_final_1__7), .in_14(siguiente_posicion_final_1_out_44),
    .in_15(siguiente_posicion_final_1__8), .in_16(siguiente_posicion_final_1_out_46),
    .in_17(siguiente_posicion_final_1__9), .in_18(siguiente_posicion_final_1_out_48),
    .in_19(siguiente_posicion_final_1__10), .in_20(siguiente_posicion_final_1_out_50),
    .in_21(siguiente_posicion_final_1__11), .in_22(siguiente_posicion_final_1_out_52),
    .in_23(siguiente_posicion_final_1__12), .in_24(siguiente_posicion_final_1_out_54),
    .in_25(siguiente_posicion_final_1__13), .in_26(siguiente_posicion_final_1_out_56),
    .in_27(siguiente_posicion_final_1__14), .in_28(siguiente_posicion_final_1_out_58),
    .in_29(siguiente_posicion_final_1__15), .in_30(siguiente_posicion_final_1_out_60),
    ._1(memoria_final_1__1), .out_32(memoria_final_1_out_32), ._2(memoria_final_1__2),
    .out_34(memoria_final_1_out_34), ._3(memoria_final_1__3), .out_36(memoria_final_1_out_36),
    ._4(memoria_final_1__4), .out_38(memoria_final_1_out_38), ._5(memoria_final_1__5),
    .out_40(memoria_final_1_out_40), ._6(memoria_final_1__6), .out_42(memoria_final_1_out_42),
    ._7(memoria_final_1__7), .out_44(memoria_final_1_out_44), ._8(memoria_final_1__8),
    .out_46(memoria_final_1_out_46), ._9(memoria_final_1__9), .out_48(memoria_final_1_out_48),
    ._10(memoria_final_1__10), .out_50(memoria_final_1_out_50), ._11(memoria_final_1__11),
    .out_52(memoria_final_1_out_52), ._12(memoria_final_1__12), .out_54(memoria_final_1_out_54),
    ._13(memoria_final_1__13), .out_56(memoria_final_1_out_56), ._14(memoria_final_1__14),
    .out_58(memoria_final_1_out_58));  // open: _15, out_60
  Salida_Final salida_final_1 (
    .in_1(in_1), .in_2(in_2), .in_3(memoria_final_1__1), .in_4(memoria_final_1_out_32),
    .in_5(memoria_final_1__2), .in_6(memoria_final_1_out_34), .in_7(memoria_final_1__3),
    .in_8(memoria_final_1_out_36), .in_9(memoria_final_1__4), .in_10(memoria_final_1_out_38),
    .in_11(memoria_final_1__5), .in_12(memoria_final_1_out_40), .in_13(memoria_final_1__6),
    .in_14(memoria_final_1_out_42), .in_15(memoria_final_1__7), .in_16(memoria_final_1_out_44),
    .in_17(memoria_final_1__8), .in_18(memoria_final_1_out_46), .in_19(memoria_final_1__9),
    .in_20(memoria_final_1_out_48), .in_21(memoria_final_1__10), .in_22(memoria_final_1_out_50),
    .in_23(memoria_final_1__11), .in_24(memoria_final_1_out_52), .in_25(memoria_final_1__12),
    .in_26(memoria_final_1_out_54), .in_27(memoria_final_1__13), .in_28(memoria_final_1_out_56),
    .in_29(memoria_final_1__14), .in_30(memoria_final_1_out_58), ._1(out_3), ._2(out_4), ._3(out_5),
    ._4(out_6), ._5(out_7), ._6(out_8), ._7(out_9), ._8(out_10), ._9(out_11), ._10(out_12), ._11(out_13),
    ._12(out_14), ._13(out_15), ._14(out_16), ._15(out_17));
endmodule

module Siguiente_Posicion_Final (
  input  [2:0] in_1,
  input  [2:0] in_2,
  input  [2:0] in_3,
  input  [2:0] in_4,
  input  [2:0] in_5,
  input  [2:0] in_6,
  input  [2:0] in_7,
  input  [2:0] in_8,
  input  [2:0] in_9,
  input  [2:0] in_10,
  input  [2:0] in_11,
  input  [2:0] in_12,
  input  [2:0] in_13,
  input  [2:0] in_14,
  input  [2:0] in_15,
  input  [2:0] in_16,
  input  [2:0] in_17,
  input  [2:0] in_18,
  input  [2:0] in_19,
  input  [2:0] in_20,
  input  [2:0] in_21,
  input  [2:0] in_22,
  input  [2:0] in_23,
  input  [2:0] in_24,
  input  [2:0] in_25,
  input  [2:0] in_26,
  input  [2:0] in_27,
  input  [2:0] in_28,
  input  [2:0] in_29,
  input  [2:0] in_30,
  output [2:0] _1,
  output [2:0] out_32,
  output [2:0] _2,
  output [2:0] out_34,
  output [2:0] _3,
  output [2:0] out_36,
  output [2:0] _4,
  output [2:0] out_38,
  output [2:0] _5,
  output [2:0] out_40,
  output [2:0] _6,
  output [2:0] out_42,
  output [2:0] _7,
  output [2:0] out_44,
  output [2:0] _8,
  output [2:0] out_46,
  output [2:0] _9,
  output [2:0] out_48,
  output [2:0] _10,
  output [2:0] out_50,
  output [2:0] _11,
  output [2:0] out_52,
  output [2:0] _12,
  output [2:0] out_54,
  output [2:0] _13,
  output [2:0] out_56,
  output [2:0] _14,
  output [2:0] out_58,
  output [2:0] _15,
  output [2:0] out_60
);

  Siguiente_Posicion siguiente_posicion_1 (.in_1(in_1), .in_2(in_2), .out_3(_1), .out_4(out_32));
  Siguiente_Posicion siguiente_posicion_2 (.in_1(in_3), .in_2(in_4), .out_3(_2), .out_4(out_34));
  Siguiente_Posicion siguiente_posicion_3 (.in_1(in_5), .in_2(in_6), .out_3(_3), .out_4(out_36));
  Siguiente_Posicion siguiente_posicion_4 (.in_1(in_7), .in_2(in_8), .out_3(_4), .out_4(out_38));
  Siguiente_Posicion siguiente_posicion_5 (.in_1(in_9), .in_2(in_10), .out_3(_5), .out_4(out_40));
  Siguiente_Posicion siguiente_posicion_6 (.in_1(in_11), .in_2(in_12), .out_3(_6), .out_4(out_42));
  Siguiente_Posicion siguiente_posicion_7 (.in_1(in_13), .in_2(in_14), .out_3(_7), .out_4(out_44));
  Siguiente_Posicion siguiente_posicion_8 (.in_1(in_15), .in_2(in_16), .out_3(_8), .out_4(out_46));
  Siguiente_Posicion siguiente_posicion_9 (.in_1(in_17), .in_2(in_18), .out_3(_9), .out_4(out_48));
  Siguiente_Posicion siguiente_posicion_10 (.in_1(in_19), .in_2(in_20), .out_3(_10), .out_4(out_50));
  Siguiente_Posicion siguiente_posicion_11 (.in_1(in_21), .in_2(in_22), .out_3(_11), .out_4(out_52));
  Siguiente_Posicion siguiente_posicion_12 (.in_1(in_23), .in_2(in_24), .out_3(_12), .out_4(out_54));
  Siguiente_Posicion siguiente_posicion_13 (.in_1(in_25), .in_2(in_26), .out_3(_13), .out_4(out_56));
  Siguiente_Posicion siguiente_posicion_14 (.in_1(in_27), .in_2(in_28), .out_3(_14), .out_4(out_58));
  Siguiente_Posicion siguiente_posicion_15 (.in_1(in_29), .in_2(in_30), .out_3(_15), .out_4(out_60));
endmodule

module Salida_Final (
  input  [2:0] in_1,
  input  [2:0] in_2,
  input  [2:0] in_3,
  input  [2:0] in_4,
  input  [2:0] in_5,
  input  [2:0] in_6,
  input  [2:0] in_7,
  input  [2:0] in_8,
  input  [2:0] in_9,
  input  [2:0] in_10,
  input  [2:0] in_11,
  input  [2:0] in_12,
  input  [2:0] in_13,
  input  [2:0] in_14,
  input  [2:0] in_15,
  input  [2:0] in_16,
  input  [2:0] in_17,
  input  [2:0] in_18,
  input  [2:0] in_19,
  input  [2:0] in_20,
  input  [2:0] in_21,
  input  [2:0] in_22,
  input  [2:0] in_23,
  input  [2:0] in_24,
  input  [2:0] in_25,
  input  [2:0] in_26,
  input  [2:0] in_27,
  input  [2:0] in_28,
  input  [2:0] in_29,
  input  [2:0] in_30,
  output [3:0] _1,
  output [3:0] _2,
  output [3:0] _3,
  output [3:0] _4,
  output [3:0] _5,
  output [3:0] _6,
  output [3:0] _7,
  output [3:0] _8,
  output [3:0] _9,
  output [3:0] _10,
  output [3:0] _11,
  output [3:0] _12,
  output [3:0] _13,
  output [3:0] _14,
  output [3:0] _15
);

  Salida salida_1 (.in_1(in_1), .in_2(in_2), .out_3(_1));
  Salida salida_2 (.in_1(in_3), .in_2(in_4), .out_3(_2));
  Salida salida_3 (.in_1(in_5), .in_2(in_6), .out_3(_3));
  Salida salida_4 (.in_1(in_7), .in_2(in_8), .out_3(_4));
  Salida salida_5 (.in_1(in_9), .in_2(in_10), .out_3(_5));
  Salida salida_6 (.in_1(in_11), .in_2(in_12), .out_3(_6));
  Salida salida_7 (.in_1(in_13), .in_2(in_14), .out_3(_7));
  Salida salida_8 (.in_1(in_15), .in_2(in_16), .out_3(_8));
  Salida salida_9 (.in_1(in_17), .in_2(in_18), .out_3(_9));
  Salida salida_10 (.in_1(in_19), .in_2(in_20), .out_3(_10));
  Salida salida_11 (.in_1(in_21), .in_2(in_22), .out_3(_11));
  Salida salida_12 (.in_1(in_23), .in_2(in_24), .out_3(_12));
  Salida salida_13 (.in_1(in_25), .in_2(in_26), .out_3(_13));
  Salida salida_14 (.in_1(in_27), .in_2(in_28), .out_3(_14));
  Salida salida_15 (.in_1(in_29), .in_2(in_30), .out_3(_15));
endmodule
